# Fritzing sketch arduino_quadcopter (saved by Fritzing 0.9.4)
breadboards: 1

parts:
  Part1 = Arduino Nano 33 IOT
  Q1 = MOSFET-NCHANNEL [package=to220v]
  M1 = DC Motor
  U1 = LIPO-1000mAh [package=lipo-1000]
  R1 = Resistor [tolerance=±5% resistance=100 package="0402 [SMD]"]
  R2 = Resistor [tolerance=±5% resistance=10k package="2512 [SMD]"]
  D1 = DIODE-SCHOTTKY [package=sma-diode]
  Q2 = MOSFET-NCHANNEL [package=to220v]
  M2 = DC Motor
  R3 = Resistor [tolerance=±5% resistance=100 package="0402 [SMD]"]
  R4 = Resistor [tolerance=±5% resistance=10k package="2512 [SMD]"]
  D2 = DIODE-SCHOTTKY [package=sma-diode]
  Q3 = MOSFET-NCHANNEL [package=to220v]
  M3 = DC Motor
  R5 = Resistor [tolerance=±5% resistance=100 package="0402 [SMD]"]
  R6 = Resistor [tolerance=±5% resistance=10k package="2512 [SMD]"]
  D3 = DIODE-SCHOTTKY [package=sma-diode]
  Q4 = MOSFET-NCHANNEL [package=to220v]
  M4 = DC Motor
  R7 = Resistor [tolerance=±5% resistance=100 package="0402 [SMD]"]
  R8 = Resistor [tolerance=±5% resistance=10k package="2512 [SMD]"]
  D4 = DIODE-SCHOTTKY [package=sma-diode]
  FLED1 = LEDs [package=led10mm]
  FLED2 = LEDs [package=led10mm]
  R9 = Resistor [tolerance=±5% resistance=10 package=THT]
  RLED1 = LEDs [package=led10mm]
  RLED2 = LEDs [package=led10mm]
  Q5 = Basic FET P-Channel [package="TO220 [THT]"]

nets:
  N1: Part1.RESET, Part1.A7
  GND: Part1.GND, Part1.D13~, Q1.S, U1.-, R2.Pin_1, Q2.S, R4.Pin_1, Q3.S, R6.Pin_1, Q4.S, R8.Pin_1, FLED1.C, FLED2.C, RLED1.C, RLED2.C, Q5.gate
  N2: Part1.D2, R1.Pin_0, R2.Pin_0
  N3: Part1.D3~, R5.Pin_0, R6.Pin_0
  N4: Part1.D5~, R3.Pin_0, R4.Pin_0
  N5: Part1.D6~, R7.Pin_0, R8.Pin_0
  N6: Part1.D10~, R9.Pin_0
  N7: Part1.D11/MOSI, Part1.+5V
  N8: Part1.VIN, M1.pin_1, D1.C, M2.pin_1, D2.C, M3.pin_1, D3.C, M4.pin_1, D4.C, Q5.source
  N9: Q1.G, R1.Pin_1
  N10: Q1.D, M1.pin_2, D1.A
  N11: U1.+, Q5.drain
  N12: Q2.G, R3.Pin_1
  N13: Q2.D, M2.pin_2, D2.A
  N14: Q3.G, R5.Pin_1
  N15: Q3.D, M3.pin_2, D3.A
  N16: Q4.G, R7.Pin_1
  N17: Q4.D, M4.pin_2, D4.A
  N18: FLED1.A, FLED2.A, R9.Pin_1, RLED1.A, RLED2.A

custom parts:
  Arduino Nano 33 IOT: The Arduino Nano 33 IoT is the easiest and cheapest point of entry to enhance existing devices (and creating new ones) to be part of the IoT and designing pico-network applications. Whether you are looking at building a sensor network connected to your office or home router, or if you want to create a BLE device sending data to a cellphone, the Nano 33 IoT is your one-stop-solution for many of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
